// Logisim project TPU.circ as structural Verilog: 18 circuits, main circuit adder_2bit
module ram2Adder (
  input  in_1,
  input  in_2
);

  wire clock_1_out;
  wire [7:0] counter_1_q, counter_2_q;
  wire [15:0] adder_16bit_1_result, ram_1_dout, ram_2_dout, register_1_q, register_2_q, register_3_q;

  Clock clock_1 (.out(clock_1_out));
  // Probe on counter_1_q
  Counter counter_1 (.Q(counter_1_q), .clk(clock_1_out));  // open: load, D, count, carry, up, clr
  RAM #(.dataWidth(16), .\type ("nonvolatile")) ram_1 (
    .addr(counter_1_q), .clk(clock_1_out), .dout(ram_1_dout));  // open: we, oe, din
  RAM #(.dataWidth(16), .\type ("nonvolatile")) ram_2 (
    .addr(counter_1_q), .clk(clock_1_out), .dout(ram_2_dout));  // open: we, oe, din
  // Probe on ram_1_dout
  // Probe on ram_2_dout
  Register #(.width(16)) register_1 (.D(ram_1_dout), .en(in_1), .clk(clock_1_out), .Q(register_1_q));  // open: clr
  Register #(.width(16)) register_2 (.D(ram_2_dout), .en(in_1), .clk(clock_1_out), .Q(register_2_q));  // open: clr
  // Probe on adder_16bit_1_result
  adder_16bit adder_16bit_1 (
    .A(register_1_q), .B(register_2_q), .Result(adder_16bit_1_result));  // open: Carry_in, Carry_out
  Register #(.width(16)) register_3 (.D(adder_16bit_1_result), .clk(clock_1_out), .Q(register_3_q));  // open: en, clr
  RAM #(.dataWidth(16)) ram_3 (.addr(counter_2_q), .we(in_2), .clk(clock_1_out), .din(register_3_q));  // open: oe, dout
  Counter counter_2 (.Q(counter_2_q), .clk(clock_1_out));  // open: load, D, count, carry, up, clr
endmodule

module ram2multiAdder (
  input  d,
  input  c,
  input  b,
  input  a,
  input  z,
  input  y,
  input  x,
  input  w,
  input  Pass1,
  input  Pass2,
  input  Pass3,
  input  Pass4
);

  wire clock_1_out, or_1_out;
  wire [7:0] counter_1_q, counter_2_q;
  wire [15:0] A1_q, A2_q, A3_q, A4_q, B1_q, B2_q, B3_q, B4_q, controlled_buffer_1_out, multiadder_16bit_1_r1,
       multiadder_16bit_1_r2, multiadder_16bit_1_r3, multiadder_16bit_1_r4, R1_q, R2_q, R3_q, R4_q,
       ram_1_dout, ram_2_dout;

  Clock clock_1 (.out(clock_1_out));
  RAM #(.dataWidth(16), .\type ("nonvolatile")) ram_1 (
    .addr(counter_1_q), .clk(clock_1_out), .dout(ram_1_dout));  // open: we, oe, din
  Counter counter_1 (.Q(counter_1_q), .clk(clock_1_out));  // open: load, D, count, carry, up, clr
  RAM #(.dataWidth(16), .\type ("nonvolatile")) ram_2 (
    .addr(counter_1_q), .clk(clock_1_out), .dout(ram_2_dout));  // open: we, oe, din
  // Probe on ram_1_dout
  // Probe on ram_2_dout
  Register #(.width(16)) A1 (.D(ram_1_dout), .en(a), .clk(clock_1_out), .Q(A1_q));  // open: clr
  Register #(.width(16)) A2 (.D(ram_1_dout), .en(b), .clk(clock_1_out), .Q(A2_q));  // open: clr
  Register #(.width(16)) A3 (.D(ram_1_dout), .en(c), .clk(clock_1_out), .Q(A3_q));  // open: clr
  Register #(.width(16)) A4 (.D(ram_1_dout), .en(d), .clk(clock_1_out), .Q(A4_q));  // open: clr
  Register #(.width(16)) B1 (.D(ram_2_dout), .en(a), .clk(clock_1_out), .Q(B1_q));  // open: clr
  Register #(.width(16)) B2 (.D(ram_2_dout), .en(b), .clk(clock_1_out), .Q(B2_q));  // open: clr
  Register #(.width(16)) B3 (.D(ram_2_dout), .en(c), .clk(clock_1_out), .Q(B3_q));  // open: clr
  Register #(.width(16)) B4 (.D(ram_2_dout), .en(d), .clk(clock_1_out), .Q(B4_q));  // open: clr
  // Probe on B1_q
  // Probe on B2_q
  // Probe on A1_q
  // Probe on A2_q
  // Probe on A3_q
  // Probe on A4_q
  // Probe on B3_q
  // Probe on B4_q
  multiadder_16bit multiadder_16bit_1 (
    .A1(A1_q), .A2(A2_q), .A3(A3_q), .A4(A4_q), .B1(B1_q), .B2(B2_q), .B3(B3_q), .B4(B4_q),
    .R1(multiadder_16bit_1_r1), .R2(multiadder_16bit_1_r2), .R3(multiadder_16bit_1_r3),
    .R4(multiadder_16bit_1_r4));  // open: C1, C2, C3, C4
  // Probe on multiadder_16bit_1_r2
  // Probe on multiadder_16bit_1_r3
  // Probe on multiadder_16bit_1_r4
  // Probe on multiadder_16bit_1_r1
  Register #(.width(16)) R1 (.D(multiadder_16bit_1_r1), .en(w), .clk(clock_1_out), .Q(R1_q));  // open: clr
  Register #(.width(16)) R2 (.D(multiadder_16bit_1_r2), .en(x), .clk(clock_1_out), .Q(R2_q));  // open: clr
  Register #(.width(16)) R3 (.D(multiadder_16bit_1_r3), .en(y), .clk(clock_1_out), .Q(R3_q));  // open: clr
  Register #(.width(16)) R4 (.D(multiadder_16bit_1_r4), .en(z), .clk(clock_1_out), .Q(R4_q));  // open: clr
  assign controlled_buffer_1_out = Pass1 ? R1_q : 16'bz;  // Controlled_Buffer controlled_buffer_1
  assign controlled_buffer_1_out = Pass2 ? R2_q : 16'bz;  // Controlled_Buffer controlled_buffer_2
  assign controlled_buffer_1_out = Pass3 ? R3_q : 16'bz;  // Controlled_Buffer controlled_buffer_3
  assign controlled_buffer_1_out = Pass4 ? R4_q : 16'bz;  // Controlled_Buffer controlled_buffer_4
  or or_1 (or_1_out, Pass1, Pass2, Pass3, Pass4);
  RAM #(.dataWidth(16)) ram_3 (
    .addr(counter_2_q), .we(or_1_out), .clk(clock_1_out), .din(controlled_buffer_1_out));  // open: oe, dout
  Counter counter_2 (.count(or_1_out), .Q(counter_2_q), .clk(clock_1_out));  // open: load, D, carry, up, clr
endmodule

module ram2multi_compractor (
);

  wire clock_1_out, comparator_1_eq, comparator_2_eq, comparator_3_eq, comparator_4_eq, comparator_5_eq,
       comparator_6_eq, comparator_7_eq, comparator_8_eq, comparator_9_eq, comparator_10_eq;
  wire [7:0] counter_1_q, counter_2_q, counter_3_q;
  wire [15:0] A1_q, A2_q, A3_q, A4_q, B1_q, B2_q, B3_q, B4_q, controlled_buffer_1_out, multiadder_16bit_1_r1,
       multiadder_16bit_1_r2, multiadder_16bit_1_r3, multiadder_16bit_1_r4, R1_q, R2_q, R3_q, R4_q,
       ram_1_dout, ram_2_dout;

  Clock clock_1 (.out(clock_1_out));
  RAM #(.dataWidth(16), .\type ("nonvolatile")) ram_1 (
    .addr(counter_1_q), .clk(clock_1_out), .dout(ram_1_dout));  // open: we, oe, din
  Counter counter_1 (.Q(counter_1_q), .clk(clock_1_out));  // open: load, D, count, carry, up, clr
  RAM #(.dataWidth(16), .\type ("nonvolatile")) ram_2 (
    .addr(counter_1_q), .clk(clock_1_out), .dout(ram_2_dout));  // open: we, oe, din
  Register #(.width(16)) A1 (.D(ram_1_dout), .en(comparator_2_eq), .clk(clock_1_out), .Q(A1_q));  // open: clr
  Register #(.width(16)) A2 (.D(ram_1_dout), .en(comparator_3_eq), .clk(clock_1_out), .Q(A2_q));  // open: clr
  Register #(.width(16)) A3 (.D(ram_1_dout), .en(comparator_4_eq), .clk(clock_1_out), .Q(A3_q));  // open: clr
  Register #(.width(16)) A4 (.D(ram_1_dout), .en(comparator_5_eq), .clk(clock_1_out), .Q(A4_q));  // open: clr
  Register #(.width(16)) B1 (.D(ram_2_dout), .en(comparator_2_eq), .clk(clock_1_out), .Q(B1_q));  // open: clr
  Register #(.width(16)) B2 (.D(ram_2_dout), .en(comparator_3_eq), .clk(clock_1_out), .Q(B2_q));  // open: clr
  Register #(.width(16)) B3 (.D(ram_2_dout), .en(comparator_4_eq), .clk(clock_1_out), .Q(B3_q));  // open: clr
  Register #(.width(16)) B4 (.D(ram_2_dout), .en(comparator_5_eq), .clk(clock_1_out), .Q(B4_q));  // open: clr
  // Probe on B1_q
  // Probe on B2_q
  // Probe on A1_q
  // Probe on A2_q
  // Probe on A3_q
  // Probe on A4_q
  // Probe on B3_q
  // Probe on B4_q
  Counter counter_2 (.Q(counter_2_q), .clk(clock_1_out), .clr(comparator_1_eq));  // open: load, D, count, carry, up
  Comparator comparator_1 (.a(8'h5), .b(counter_2_q), .eq(comparator_1_eq));  // open: gt, lt
  Comparator comparator_2 (.a(8'h1), .b(counter_2_q), .eq(comparator_2_eq));  // open: gt, lt
  Comparator comparator_3 (.a(8'h2), .b(counter_2_q), .eq(comparator_3_eq));  // open: gt, lt
  Comparator comparator_4 (.a(8'h3), .b(counter_2_q), .eq(comparator_4_eq));  // open: gt, lt
  Comparator comparator_5 (.a(8'h4), .b(counter_2_q), .eq(comparator_5_eq));  // open: gt, lt
  multiadder_16bit multiadder_16bit_1 (
    .A1(A1_q), .A2(A2_q), .A3(A3_q), .A4(A4_q), .B1(B1_q), .B2(B2_q), .B3(B3_q), .B4(B4_q),
    .R1(multiadder_16bit_1_r1), .R2(multiadder_16bit_1_r2), .R3(multiadder_16bit_1_r3),
    .R4(multiadder_16bit_1_r4));  // open: C1, C2, C3, C4
  // Probe on multiadder_16bit_1_r1
  // Probe on multiadder_16bit_1_r2
  // Probe on multiadder_16bit_1_r3
  // Probe on multiadder_16bit_1_r4
  Register #(.width(16)) R1 (.D(multiadder_16bit_1_r1), .clk(clock_1_out), .Q(R1_q));  // open: en, clr
  Register #(.width(16)) R2 (.D(multiadder_16bit_1_r2), .clk(clock_1_out), .Q(R2_q));  // open: en, clr
  Register #(.width(16)) R3 (.D(multiadder_16bit_1_r3), .clk(clock_1_out), .Q(R3_q));  // open: en, clr
  Register #(.width(16)) R4 (.D(multiadder_16bit_1_r4), .clk(clock_1_out), .Q(R4_q));  // open: en, clr
  Comparator comparator_6 (.a(8'h1), .b(counter_3_q), .eq(comparator_6_eq));  // open: gt, lt
  Comparator comparator_7 (.a(8'h2), .b(counter_3_q), .eq(comparator_7_eq));  // open: gt, lt
  Comparator comparator_8 (.a(8'h3), .b(counter_3_q), .eq(comparator_8_eq));  // open: gt, lt
  Comparator comparator_9 (.a(8'h4), .b(counter_3_q), .eq(comparator_9_eq));  // open: gt, lt
  assign controlled_buffer_1_out = comparator_6_eq ? R1_q : 16'bz;  // Controlled_Buffer controlled_buffer_1
  assign controlled_buffer_1_out = comparator_7_eq ? R2_q : 16'bz;  // Controlled_Buffer controlled_buffer_2
  assign controlled_buffer_1_out = comparator_8_eq ? R3_q : 16'bz;  // Controlled_Buffer controlled_buffer_3
  assign controlled_buffer_1_out = comparator_9_eq ? R4_q : 16'bz;  // Controlled_Buffer controlled_buffer_4
  Counter counter_3 (.Q(counter_3_q), .clk(clock_1_out), .clr(comparator_10_eq));  // open: load, D, count, carry, up
  Comparator comparator_10 (.a(8'h3), .b(counter_1_q), .eq(comparator_10_eq));  // open: gt, lt
  RAM #(.dataWidth(16)) ram_3 (
    .addr(counter_1_q), .clk(clock_1_out), .din(controlled_buffer_1_out));  // open: we, oe, dout
endmodule

module ram2multiadder_auto (
);

  wire clock_1_out, or_1_out, or_2_out;
  wire [3:0] counter_1_q, counter_1_q_2;
  wire [7:0] counter_2_q, counter_3_q;
  wire [15:0] A1_q, A2_q, A3_q, A4_q, B1_q, B2_q, B3_q, B4_q, controlled_buffer_1_out, multiadder_16bit_1_r1,
       multiadder_16bit_1_r2, multiadder_16bit_1_r3, multiadder_16bit_1_r4, R1_q, R2_q, R3_q, R4_q,
       ram_1_dout, ram_2_dout, RomCPU_data;

  or or_1 (or_1_out, RomCPU_data[11], RomCPU_data[10], RomCPU_data[9], RomCPU_data[8]);
  Clock clock_1 (.out(clock_1_out));
  RAM #(.dataWidth(16), .\type ("nonvolatile")) ram_1 (
    .addr({counter_1_q_2, counter_1_q}), .clk(clock_1_out), .dout(ram_1_dout));  // open: we, oe, din
  Counter counter_1 (
    .count(or_1_out), .Q({counter_1_q_2, counter_1_q}), .clk(clock_1_out));  // open: load, D, carry, up, clr
  RAM #(.dataWidth(16), .\type ("nonvolatile")) ram_2 (
    .addr({counter_1_q_2, counter_1_q}), .clk(clock_1_out), .dout(ram_2_dout));  // open: we, oe, din
  // Probe on ram_1_dout
  // Probe on ram_2_dout
  Register #(.width(16)) A1 (.D(ram_1_dout), .en(RomCPU_data[15]), .clk(clock_1_out), .Q(A1_q));  // open: clr
  Register #(.width(16)) A2 (.D(ram_1_dout), .en(RomCPU_data[14]), .clk(clock_1_out), .Q(A2_q));  // open: clr
  Register #(.width(16)) A3 (.D(ram_1_dout), .en(RomCPU_data[13]), .clk(clock_1_out), .Q(A3_q));  // open: clr
  Register #(.width(16)) A4 (.D(ram_1_dout), .en(RomCPU_data[12]), .clk(clock_1_out), .Q(A4_q));  // open: clr
  Register #(.width(16)) B1 (.D(ram_2_dout), .en(RomCPU_data[11]), .clk(clock_1_out), .Q(B1_q));  // open: clr
  Register #(.width(16)) B2 (.D(ram_2_dout), .en(RomCPU_data[10]), .clk(clock_1_out), .Q(B2_q));  // open: clr
  Register #(.width(16)) B3 (.D(ram_2_dout), .en(RomCPU_data[9]), .clk(clock_1_out), .Q(B3_q));  // open: clr
  Register #(.width(16)) B4 (.D(ram_2_dout), .en(RomCPU_data[8]), .clk(clock_1_out), .Q(B4_q));  // open: clr
  // Probe on B1_q
  // Probe on B2_q
  // Probe on A1_q
  // Probe on A2_q
  // Probe on A3_q
  // Probe on A4_q
  // Probe on B3_q
  // Probe on B4_q
  Hex_Digit_Display hex_digit_display_1 (.value(counter_1_q_2));  // open: dp
  Hex_Digit_Display hex_digit_display_2 (.value(counter_1_q));  // open: dp
  multiadder_16bit multiadder_16bit_1 (
    .A1(A1_q), .A2(A2_q), .A3(A3_q), .A4(A4_q), .B1(B1_q), .B2(B2_q), .B3(B3_q), .B4(B4_q),
    .R1(multiadder_16bit_1_r1), .R2(multiadder_16bit_1_r2), .R3(multiadder_16bit_1_r3),
    .R4(multiadder_16bit_1_r4));  // open: C1, C2, C3, C4
  // Probe on multiadder_16bit_1_r1
  // Probe on multiadder_16bit_1_r2
  // Probe on multiadder_16bit_1_r3
  // Probe on multiadder_16bit_1_r4
  Register #(.width(16)) R1 (.D(multiadder_16bit_1_r1), .en(RomCPU_data[7]), .clk(clock_1_out), .Q(R1_q));  // open: clr
  Register #(.width(16)) R2 (.D(multiadder_16bit_1_r2), .en(RomCPU_data[6]), .clk(clock_1_out), .Q(R2_q));  // open: clr
  Register #(.width(16)) R3 (.D(multiadder_16bit_1_r3), .en(RomCPU_data[5]), .clk(clock_1_out), .Q(R3_q));  // open: clr
  Register #(.width(16)) R4 (.D(multiadder_16bit_1_r4), .en(RomCPU_data[4]), .clk(clock_1_out), .Q(R4_q));  // open: clr
  Counter counter_2 (.Q(counter_2_q), .clk(clock_1_out));  // open: load, D, count, carry, up, clr
  assign controlled_buffer_1_out = RomCPU_data[3] ? R1_q : 16'bz;  // Controlled_Buffer controlled_buffer_1
  assign controlled_buffer_1_out = RomCPU_data[2] ? R2_q : 16'bz;  // Controlled_Buffer controlled_buffer_2
  ROM #(.dataWidth(16)) RomCPU (.addr(counter_2_q), .data(RomCPU_data));
  assign controlled_buffer_1_out = RomCPU_data[1] ? R3_q : 16'bz;  // Controlled_Buffer controlled_buffer_3
  assign controlled_buffer_1_out = RomCPU_data[0] ? R4_q : 16'bz;  // Controlled_Buffer controlled_buffer_4
  // Probe on controlled_buffer_1_out
  // Probe on controlled_buffer_1_out
  // Probe on controlled_buffer_1_out
  // Probe on controlled_buffer_1_out
  or or_2 (or_2_out, RomCPU_data[0], RomCPU_data[1], RomCPU_data[2], RomCPU_data[3]);
  Counter counter_3 (.count(or_2_out), .Q(counter_3_q), .clk(clock_1_out));  // open: load, D, carry, up, clr
  // Probe on counter_3_q
  RAM #(.dataWidth(16)) ram_3 (
    .addr(counter_3_q), .we(or_2_out), .clk(clock_1_out), .din(controlled_buffer_1_out));  // open: oe, dout

  // Notes on the sheet:
  //   contents of RomCPU (hex, n*v repeats v):
  //   0 8800 4480 2248 1124 8812 4481
endmodule

module sumofsum_auto (
);

  wire clock_1_out, or_1_out;
  wire [7:0] counter_1_q, counter_2_q, counter_3_q, counter_4_q, counter_5_q;
  wire [15:0] A1_q, A2_q, A3_q, A4_q, B1_q, B2_q, B3_q, B4_q, controlled_buffer_1_out,
       controlled_buffer_5_out, multiadder_16bit_1_r1, multiadder_16bit_1_r2, multiadder_16bit_1_r3,
       multiadder_16bit_1_r4, R1_q, R2_q, R3_q, R4_q, ram_1_dout, ram_2_dout, register_1_q, register_2_q,
       register_3_q, register_4_q, register_5_q, rom_1_data, sum_4val_1_result;

  Clock clock_1 (.out(clock_1_out));
  RAM #(.dataWidth(16), .\type ("nonvolatile")) ram_1 (
    .addr(counter_1_q), .clk(clock_1_out), .dout(ram_1_dout));  // open: we, oe, din
  // Probe on counter_1_q
  Counter counter_1 (.Q(counter_1_q), .clk(clock_1_out));  // open: load, D, count, carry, up, clr
  RAM #(.dataWidth(16), .\type ("nonvolatile")) ram_2 (
    .addr(counter_1_q), .clk(clock_1_out), .dout(ram_2_dout));  // open: we, oe, din
  // Probe on ram_1_dout
  // Probe on ram_2_dout
  Register #(.width(16)) A1 (.D(ram_1_dout), .en(rom_1_data[15]), .clk(clock_1_out), .Q(A1_q));  // open: clr
  Register #(.width(16)) A2 (.D(ram_1_dout), .en(rom_1_data[14]), .clk(clock_1_out), .Q(A2_q));  // open: clr
  Register #(.width(16)) A3 (.D(ram_1_dout), .en(rom_1_data[13]), .clk(clock_1_out), .Q(A3_q));  // open: clr
  Register #(.width(16)) A4 (.D(ram_1_dout), .en(rom_1_data[12]), .clk(clock_1_out), .Q(A4_q));  // open: clr
  Register #(.width(16)) B1 (.D(ram_2_dout), .en(rom_1_data[11]), .clk(clock_1_out), .Q(B1_q));  // open: clr
  Register #(.width(16)) B2 (.D(ram_2_dout), .en(rom_1_data[10]), .clk(clock_1_out), .Q(B2_q));  // open: clr
  Register #(.width(16)) B3 (.D(ram_2_dout), .en(rom_1_data[9]), .clk(clock_1_out), .Q(B3_q));  // open: clr
  Register #(.width(16)) B4 (.D(ram_2_dout), .en(rom_1_data[8]), .clk(clock_1_out), .Q(B4_q));  // open: clr
  // Probe on A1_q
  // Probe on A2_q
  // Probe on A3_q
  // Probe on A4_q
  // Probe on B1_q
  // Probe on B2_q
  // Probe on B3_q
  // Probe on B4_q
  multiadder_16bit multiadder_16bit_1 (
    .A1(A1_q), .A2(A2_q), .A3(A3_q), .A4(A4_q), .B1(B1_q), .B2(B2_q), .B3(B3_q), .B4(B4_q),
    .R1(multiadder_16bit_1_r1), .R2(multiadder_16bit_1_r2), .R3(multiadder_16bit_1_r3),
    .R4(multiadder_16bit_1_r4));  // open: C1, C2, C3, C4
  // Probe on multiadder_16bit_1_r1
  // Probe on multiadder_16bit_1_r2
  // Probe on multiadder_16bit_1_r3
  // Probe on multiadder_16bit_1_r4
  Register #(.width(16)) R1 (.D(multiadder_16bit_1_r1), .en(rom_1_data[7]), .clk(clock_1_out), .Q(R1_q));  // open: clr
  Register #(.width(16)) R2 (.D(multiadder_16bit_1_r2), .en(rom_1_data[6]), .clk(clock_1_out), .Q(R2_q));  // open: clr
  Register #(.width(16)) R3 (.D(multiadder_16bit_1_r3), .en(rom_1_data[5]), .clk(clock_1_out), .Q(R3_q));  // open: clr
  Register #(.width(16)) R4 (.D(multiadder_16bit_1_r4), .en(rom_1_data[4]), .clk(clock_1_out), .Q(R4_q));  // open: clr
  assign controlled_buffer_1_out = rom_1_data[3] ? R1_q : 16'bz;  // Controlled_Buffer controlled_buffer_1
  assign controlled_buffer_1_out = rom_1_data[2] ? R2_q : 16'bz;  // Controlled_Buffer controlled_buffer_2
  ROM #(.dataWidth(16)) rom_1 (.addr(counter_2_q), .data(rom_1_data));
  Counter counter_2 (.Q(counter_2_q), .clk(clock_1_out));  // open: load, D, count, carry, up, clr
  assign controlled_buffer_1_out = rom_1_data[1] ? R3_q : 16'bz;  // Controlled_Buffer controlled_buffer_3
  assign controlled_buffer_1_out = rom_1_data[0] ? R4_q : 16'bz;  // Controlled_Buffer controlled_buffer_4
  // Probe on controlled_buffer_1_out
  // Probe on controlled_buffer_1_out
  // Probe on controlled_buffer_1_out
  // Probe on controlled_buffer_1_out
  or or_1 (or_1_out, rom_1_data[0], rom_1_data[1], rom_1_data[2], rom_1_data[3]);
  RAM #(.dataWidth(16)) ram_3 (
    .addr(counter_3_q), .we(or_1_out), .clk(clock_1_out), .din(controlled_buffer_1_out));  // open: oe, dout
  Counter counter_3 (.count(or_1_out), .Q(counter_3_q), .clk(clock_1_out));  // open: load, D, carry, up, clr
  // Probe on counter_3_q
  Register #(.width(16)) register_1 (.D(R1_q), .en(rom_1_data[3]), .clk(rom_1_data[3]), .Q(register_1_q));  // open: clr
  Register #(.width(16)) register_2 (.D(R2_q), .en(rom_1_data[2]), .clk(rom_1_data[2]), .Q(register_2_q));  // open: clr
  Register #(.width(16)) register_3 (.D(R3_q), .en(rom_1_data[1]), .clk(rom_1_data[1]), .Q(register_3_q));  // open: clr
  Register #(.width(16)) register_4 (.D(R4_q), .en(rom_1_data[0]), .clk(rom_1_data[0]), .Q(register_4_q));  // open: clr
  sum_4val sum_4val_1 (
    .sum1(register_1_q), .sum2(register_2_q), .sum3(register_3_q), .sum4(register_4_q),
    .result(sum_4val_1_result));  // open: carry
  Register #(.width(16)) register_5 (
    .D(controlled_buffer_5_out), .en(rom_1_data[0]), .clk(rom_1_data[0]), .Q(register_5_q));  // open: clr
  assign controlled_buffer_5_out = rom_1_data[0] ? sum_4val_1_result : 16'bz;  // Controlled_Buffer controlled_buffer_5
  Counter counter_4 (.Q(counter_4_q), .clk(rom_1_data[3]));  // open: load, D, count, carry, up, clr
  Counter counter_5 (.D(counter_4_q), .Q(counter_5_q), .clk(rom_1_data[3]));  // open: load, count, carry, up, clr
  RAM #(.dataWidth(16)) RamD (
    .addr(counter_5_q), .we(clock_1_out), .clk(clock_1_out), .din(register_5_q));  // open: oe, dout

  // Notes on the sheet:
  //   contents of rom_1 (hex, n*v repeats v):
  //   0 8800 4480 2248 1124 8812 4481
endmodule

module matMult_gausian (
);

  wire clock_1_out, or_1_out, or_2_out, or_3_out;
  wire [3:0] counter_3_q, counter_3_q_2;
  wire [7:0] counter_1_q, counter_2_q, counter_4_q;
  wire [15:0] A1_q, A2_q, A3_q, A4_q, B1_q, B2_q, B3_q, B4_q, C1_q, controlled_buffer_1_out,
       matmult_4x4_1_element, ram_1_dout, ram_2_dout, rom_1_data;

  or or_1 (or_1_out, rom_1_data[15], rom_1_data[14], rom_1_data[13], rom_1_data[12]);
  Clock clock_1 (.out(clock_1_out));
  or or_2 (or_2_out, rom_1_data[8], rom_1_data[9], rom_1_data[10], rom_1_data[11]);
  Counter counter_1 (.count(or_1_out), .Q(counter_1_q), .clk(clock_1_out));  // open: load, D, carry, up, clr
  RAM #(.dataWidth(16), .\type ("nonvolatile")) ram_1 (
    .addr(counter_1_q), .oe(or_1_out), .clk(clock_1_out), .dout(ram_1_dout));  // open: we, din
  Counter #(.max('hf)) counter_2 (
    .count(or_2_out), .Q(counter_2_q), .clk(clock_1_out));  // open: load, D, carry, up, clr
  RAM #(.dataWidth(16), .\type ("nonvolatile")) ram_2 (
    .addr(counter_2_q), .clk(clock_1_out), .dout(ram_2_dout));  // open: we, oe, din
  // Probe on ram_1_dout
  // Probe on ram_2_dout
  Register #(.width(16)) A1 (.D(ram_1_dout), .en(rom_1_data[15]), .clk(clock_1_out), .Q(A1_q));  // open: clr
  Register #(.width(16)) A2 (.D(ram_1_dout), .en(rom_1_data[14]), .clk(clock_1_out), .Q(A2_q));  // open: clr
  Register #(.width(16)) A3 (.D(ram_1_dout), .en(rom_1_data[13]), .clk(clock_1_out), .Q(A3_q));  // open: clr
  Register #(.width(16)) A4 (.D(ram_1_dout), .en(rom_1_data[12]), .clk(clock_1_out), .Q(A4_q));  // open: clr
  Register #(.width(16)) B1 (.D(ram_2_dout), .en(rom_1_data[11]), .clk(clock_1_out), .Q(B1_q));  // open: clr
  Register #(.width(16)) B2 (.D(ram_2_dout), .en(rom_1_data[10]), .clk(clock_1_out), .Q(B2_q));  // open: clr
  Register #(.width(16)) B3 (.D(ram_2_dout), .en(rom_1_data[9]), .clk(clock_1_out), .Q(B3_q));  // open: clr
  Register #(.width(16)) B4 (.D(ram_2_dout), .en(rom_1_data[8]), .clk(clock_1_out), .Q(B4_q));  // open: clr
  // Probe on A1_q
  // Probe on A2_q
  // Probe on A3_q
  // Probe on A4_q
  // Probe on B1_q
  // Probe on B2_q
  // Probe on B3_q
  // Probe on B4_q
  Hex_Digit_Display hex_digit_display_1 (.value(counter_3_q_2));  // open: dp
  Hex_Digit_Display hex_digit_display_2 (.value(counter_3_q));  // open: dp
  matMult_4x4 matmult_4x4_1 (
    .row1(A1_q), .row2(A2_q), .row3(A3_q), .row4(A4_q), .col1(B1_q), .col2(B2_q), .col3(B3_q), .col4(B4_q),
    .Element(matmult_4x4_1_element));  // open: carryout
  // Probe on matmult_4x4_1_element
  Register #(.width(16)) C1 (.D(matmult_4x4_1_element), .en(rom_1_data[7]), .clk(clock_1_out), .Q(C1_q));  // open: clr
  assign controlled_buffer_1_out = rom_1_data[3] ? C1_q : 16'bz;  // Controlled_Buffer controlled_buffer_1
  ROM #(.dataWidth(16)) rom_1 (.addr({counter_3_q_2, counter_3_q}), .data(rom_1_data));
  Counter counter_3 (.Q({counter_3_q_2, counter_3_q}), .clk(clock_1_out));  // open: load, D, count, carry, up, clr
  // Probe on controlled_buffer_1_out
  or or_3 (or_3_out, rom_1_data[0], rom_1_data[1], rom_1_data[2], rom_1_data[3]);
  RAM #(.dataWidth(16)) ram_3 (
    .addr(counter_4_q), .we(or_3_out), .clk(clock_1_out), .din(controlled_buffer_1_out));  // open: oe, dout
  Counter counter_4 (.count(or_3_out), .Q(counter_4_q), .clk(clock_1_out));  // open: load, D, carry, up, clr
  // Probe on counter_4_q

  // Notes on the sheet:
  //   contents of rom_1 (hex, n*v repeats v):
  //   8800 8800 4400 2200 1100 880 408 200 100 880 408 200 100 880 408 200 100 8880 4408 2200 1100 880 408
  //   200 100 880 408 200 100 880 408 200 100 8880 4408 2200 1100 880 408 200 100 880 408 200 100 880 408
  //   200 100 8880 4408 2200 1100 880 408 200 100 880 408 200 100 880 408 200 100 80 8
endmodule

module matmult_tiling (
  input  in_1
);

  wire clock_1_out, or_1_out, or_2_out;
  wire [3:0] counter_3_q, counter_3_q_2;
  wire [7:0] counter_1_q, counter_2_q, counter_4_q;
  wire [15:0] A1_q, A2_q, A3_q, A4_q, adder_1_out, B1_q, B2_q, B3_q, B4_q, controlled_buffer_1_out,
       controlled_buffer_2_out, controlled_buffer_3_out, controlled_buffer_4_out, controlled_buffer_5_out,
       controlled_buffer_6_out, controlled_buffer_7_out, controlled_buffer_8_out, matmulttile_1_c1,
       matmulttile_1_c2, matmulttile_1_c3, matmulttile_1_c4, R1_q, R2_q, R3_q, R4_q, ram_1_dout, ram_2_dout,
       register_1_q, RomCPU_data, S1_q, S2_q, S3_q, S4_q;

  Clock clock_1 (.out(clock_1_out));
  or or_1 (or_1_out, RomCPU_data[15], RomCPU_data[14], RomCPU_data[13], RomCPU_data[12]);
  RAM #(.dataWidth(16), .\type ("nonvolatile")) ram_1 (
    .addr(counter_1_q), .clk(clock_1_out), .dout(ram_1_dout));  // open: we, oe, din
  Counter counter_1 (
    .D(8'hf), .count(or_1_out), .Q(counter_1_q), .clk(clock_1_out), .clr(RomCPU_data[1]));  // open: load, carry, up
  RAM #(.dataWidth(16), .\type ("nonvolatile")) ram_2 (
    .addr(counter_2_q), .clk(clock_1_out), .dout(ram_2_dout));  // open: we, oe, din
  Counter #(.max('hf)) counter_2 (
    .count(or_1_out), .Q(counter_2_q), .clk(clock_1_out));  // open: load, D, carry, up, clr
  // Probe on ram_1_dout
  // Probe on ram_2_dout
  Register #(.width(16)) A1 (.D(ram_1_dout), .en(RomCPU_data[15]), .clk(clock_1_out), .Q(A1_q));  // open: clr
  Register #(.width(16)) A2 (.D(ram_1_dout), .en(RomCPU_data[14]), .clk(clock_1_out), .Q(A2_q));  // open: clr
  Register #(.width(16)) A3 (.D(ram_1_dout), .en(RomCPU_data[13]), .clk(clock_1_out), .Q(A3_q));  // open: clr
  Register #(.width(16)) A4 (.D(ram_1_dout), .en(RomCPU_data[12]), .clk(clock_1_out), .Q(A4_q));  // open: clr
  Register #(.width(16)) B1 (.D(ram_2_dout), .en(RomCPU_data[15]), .clk(clock_1_out), .Q(B1_q));  // open: clr
  Register #(.width(16)) B2 (.D(ram_2_dout), .en(RomCPU_data[14]), .clk(clock_1_out), .Q(B2_q));  // open: clr
  Register #(.width(16)) B3 (.D(ram_2_dout), .en(RomCPU_data[13]), .clk(clock_1_out), .Q(B3_q));  // open: clr
  Register #(.width(16)) B4 (.D(ram_2_dout), .en(RomCPU_data[12]), .clk(clock_1_out), .Q(B4_q));  // open: clr
  // Probe on A1_q
  // Probe on A2_q
  // Probe on A3_q
  // Probe on A4_q
  // Probe on B1_q
  // Probe on B2_q
  // Probe on B3_q
  // Probe on B4_q
  Hex_Digit_Display hex_digit_display_1 (.value(counter_3_q_2));  // open: dp
  Hex_Digit_Display hex_digit_display_2 (.value(counter_3_q));  // open: dp
  matMultTile matmulttile_1 (
    .A1(A1_q), .B1(A2_q), .A2(A3_q), .B3(A4_q), .B2(B1_q), .B4(B2_q), .A3(B3_q), .A4(B4_q),
    .C1(matmulttile_1_c1), .C2(matmulttile_1_c2), .C3(matmulttile_1_c3), .C4(matmulttile_1_c4));
  // Probe on matmulttile_1_c4
  Register #(.width(16)) R1 (.D(matmulttile_1_c1), .en(RomCPU_data[11]), .clk(clock_1_out), .Q(R1_q));  // open: clr
  // Probe on matmulttile_1_c1
  Register #(.width(16)) R2 (.D(matmulttile_1_c2), .en(RomCPU_data[11]), .clk(clock_1_out), .Q(R2_q));  // open: clr
  // Probe on matmulttile_1_c2
  Register #(.width(16)) R3 (.D(matmulttile_1_c3), .en(RomCPU_data[11]), .clk(clock_1_out), .Q(R3_q));  // open: clr
  // Probe on matmulttile_1_c3
  Register #(.width(16)) R4 (.D(matmulttile_1_c4), .en(RomCPU_data[11]), .clk(clock_1_out), .Q(R4_q));  // open: clr
  Register #(.width(16)) S1 (.D(matmulttile_1_c1), .en(RomCPU_data[10]), .clk(clock_1_out), .Q(S1_q));  // open: clr
  // Probe on matmulttile_1_c1
  Register #(.width(16)) S2 (.D(matmulttile_1_c2), .en(RomCPU_data[10]), .clk(clock_1_out), .Q(S2_q));  // open: clr
  // Probe on matmulttile_1_c2
  Register #(.width(16)) S3 (.D(matmulttile_1_c3), .en(RomCPU_data[10]), .clk(clock_1_out), .Q(S3_q));  // open: clr
  // Probe on matmulttile_1_c3
  Register #(.width(16)) S4 (.D(matmulttile_1_c4), .en(RomCPU_data[10]), .clk(clock_1_out), .Q(S4_q));  // open: clr
  // Probe on matmulttile_1_c4
  Counter counter_3 (.Q({counter_3_q_2, counter_3_q}), .clk(clock_1_out));  // open: load, D, count, carry, up, clr
  assign controlled_buffer_1_out = RomCPU_data[7] ? R1_q : 16'bz;  // Controlled_Buffer controlled_buffer_1
  assign controlled_buffer_2_out = RomCPU_data[6] ? R2_q : 16'bz;  // Controlled_Buffer controlled_buffer_2
  assign controlled_buffer_3_out = RomCPU_data[5] ? R3_q : 16'bz;  // Controlled_Buffer controlled_buffer_3
  assign controlled_buffer_4_out = RomCPU_data[7] ? S1_q : 16'bz;  // Controlled_Buffer controlled_buffer_4
  assign controlled_buffer_5_out = RomCPU_data[6] ? S2_q : 16'bz;  // Controlled_Buffer controlled_buffer_5
  assign controlled_buffer_6_out = RomCPU_data[5] ? S3_q : 16'bz;  // Controlled_Buffer controlled_buffer_6
  // Probe on controlled_buffer_1_out
  // Probe on controlled_buffer_2_out
  // Probe on controlled_buffer_3_out
  // Probe on controlled_buffer_7_out
  assign controlled_buffer_7_out = RomCPU_data[4] ? R4_q : 16'bz;  // Controlled_Buffer controlled_buffer_7
  // Probe on controlled_buffer_4_out
  // Probe on controlled_buffer_5_out
  // Probe on controlled_buffer_6_out
  // Probe on controlled_buffer_8_out
  assign controlled_buffer_8_out = RomCPU_data[4] ? S4_q : 16'bz;  // Controlled_Buffer controlled_buffer_8
  ROM #(.dataWidth(16)) RomCPU (.addr({counter_3_q_2, counter_3_q}), .data(RomCPU_data));
  Adder #(.width(16)) adder_1 (
    .a(controlled_buffer_1_out), .b(controlled_buffer_4_out), .out(adder_1_out));  // open: cin, cout
  Adder #(.width(16)) adder_2 (
    .a(controlled_buffer_2_out), .b(controlled_buffer_5_out), .out(adder_1_out));  // open: cin, cout
  Adder #(.width(16)) adder_3 (
    .a(controlled_buffer_3_out), .b(controlled_buffer_6_out), .out(adder_1_out));  // open: cin, cout
  Adder #(.width(16)) adder_4 (
    .a(controlled_buffer_7_out), .b(controlled_buffer_8_out), .out(adder_1_out));  // open: cin, cout
  // Probe on adder_1_out
  Counter counter_4 (.count(or_2_out), .Q(counter_4_q), .clk(clock_1_out));  // open: load, D, carry, up, clr
  or or_2 (or_2_out, in_1, RomCPU_data[6], RomCPU_data[5], RomCPU_data[4]);
  Register #(.width(16)) register_1 (
    .D(adder_1_out), .en(RomCPU_data[0]), .clk(clock_1_out), .Q(register_1_q));  // open: clr
  RAM #(.dataWidth(16)) ram_3 (
    .addr(counter_4_q), .we(RomCPU_data[0]), .clk(clock_1_out), .din(register_1_q));  // open: oe, dout

  // Notes on the sheet:
  //   contents of RomCPU (hex, n*v repeats v):
  //   8000 8000 4000 2000 1000 8800 4000 2000 1000 400 81 41 21 11 8001 8000 4000 2000 8100 4000 2000 1000
  //   10 18 14 a 9 8000 8000 4000 2000 1000 8100 4000 2000 1000 30 18 14 a 9 8000 8000 4000 2000 1000 8100
  //   4000 2000 1000 30 18 14 a 9
endmodule

module matMult_4x4 (
  input  [15:0] row1,
  input  [15:0] row2,
  input  [15:0] row3,
  input  [15:0] row4,
  input  [15:0] col1,
  input  [15:0] col2,
  input  [15:0] col3,
  input  [15:0] col4,
  output [15:0] Element,
  output carryout
);

  wire [15:0] adder_1_out, adder_2_out, multiplier_1_out, multiplier_2_out, multiplier_3_out,
       multiplier_4_out;

  Multiplier #(.width(16)) multiplier_1 (.a(row1), .b(col1), .out(multiplier_1_out));  // open: cin, cout
  Multiplier #(.width(16)) multiplier_2 (.a(row2), .b(col2), .out(multiplier_2_out));  // open: cin, cout
  Multiplier #(.width(16)) multiplier_3 (.a(row3), .b(col3), .out(multiplier_3_out));  // open: cin, cout
  Multiplier #(.width(16)) multiplier_4 (.a(row4), .b(col4), .out(multiplier_4_out));  // open: cin, cout
  Adder #(.width(16)) adder_1 (.a(multiplier_1_out), .b(multiplier_2_out), .out(adder_1_out));  // open: cin, cout
  Adder #(.width(16)) adder_2 (.a(multiplier_3_out), .b(multiplier_4_out), .out(adder_2_out));  // open: cin, cout
  Adder #(.width(16)) adder_3 (.a(adder_1_out), .b(adder_2_out), .out(Element), .cout(carryout));  // open: cin
endmodule

module matMultTile (
  input  [15:0] A1,
  input  [15:0] B1,
  input  [15:0] A2,
  input  [15:0] B3,
  input  [15:0] B2,
  input  [15:0] B4,
  input  [15:0] A3,
  input  [15:0] A4,
  output [15:0] C1,
  output [15:0] C2,
  output [15:0] C3,
  output [15:0] C4
);

  wire [15:0] multiplier_1_out, multiplier_2_out, multiplier_3_out, multiplier_4_out, multiplier_5_out,
       multiplier_6_out, multiplier_7_out, multiplier_8_out;

  Multiplier #(.width(16)) multiplier_1 (.a(A1), .b(B1), .out(multiplier_1_out));  // open: cin, cout
  Multiplier #(.width(16)) multiplier_2 (.a(A2), .b(B3), .out(multiplier_2_out));  // open: cin, cout
  Multiplier #(.width(16)) multiplier_3 (.a(A1), .b(B2), .out(multiplier_3_out));  // open: cin, cout
  Multiplier #(.width(16)) multiplier_4 (.a(A2), .b(B4), .out(multiplier_4_out));  // open: cin, cout
  Multiplier #(.width(16)) multiplier_5 (.a(A3), .b(B1), .out(multiplier_5_out));  // open: cin, cout
  Multiplier #(.width(16)) multiplier_6 (.a(A4), .b(B3), .out(multiplier_6_out));  // open: cin, cout
  Multiplier #(.width(16)) multiplier_7 (.a(A3), .b(B2), .out(multiplier_7_out));  // open: cin, cout
  Multiplier #(.width(16)) multiplier_8 (.a(A4), .b(A4), .out(multiplier_8_out));  // open: cin, cout
  Adder #(.width(16)) adder_1 (.a(multiplier_1_out), .b(multiplier_2_out), .out(C1));  // open: cin, cout
  Adder #(.width(16)) adder_2 (.a(multiplier_3_out), .b(multiplier_4_out), .out(C2));  // open: cin, cout
  Adder #(.width(16)) adder_3 (.a(multiplier_5_out), .b(multiplier_6_out), .out(C3));  // open: cin, cout
  Adder #(.width(16)) adder_4 (.a(multiplier_7_out), .b(multiplier_8_out), .out(C4));  // open: cin, cout
endmodule

module adder_16bit (
  input  Carry_in,
  input  [15:0] A,
  input  [15:0] B,
  output [15:0] Result,
  output Carry_out
);

  wire adder_8bit_1_carry_out;

  // Probe on A
  // Probe on B
  // Probe on Result
  adder_8bit adder_8bit_1 (
    .Carry_in(Carry_in), .A(A[7:0]), .B(B[7:0]), .Result(Result[7:0]), .Carry_out(adder_8bit_1_carry_out));
  adder_8bit adder_8bit_2 (
    .Carry_in(adder_8bit_1_carry_out), .A(A[15:8]), .B(B[15:8]), .Result(Result[15:8]), .Carry_out(Carry_out));
  // Probe on Carry_out
endmodule

module multiadder_16bit (
  input  [15:0] A1,
  input  [15:0] A2,
  input  [15:0] A3,
  input  [15:0] A4,
  input  [15:0] B1,
  input  [15:0] B2,
  input  [15:0] B3,
  input  [15:0] B4,
  output [15:0] R1,
  output [15:0] R2,
  output [15:0] R3,
  output [15:0] R4,
  output C1,
  output C2,
  output C3,
  output C4
);

  adder_16bit adder_16bit_1 (.A(A1), .B(B1), .Result(R1), .Carry_out(C1));  // open: Carry_in
  adder_16bit adder_16bit_2 (.A(A2), .B(B2), .Result(R2), .Carry_out(C2));  // open: Carry_in
  adder_16bit adder_16bit_3 (.A(A3), .B(B3), .Result(R3), .Carry_out(C3));  // open: Carry_in
  adder_16bit adder_16bit_4 (.A(A4), .B(B4), .Result(R4), .Carry_out(C4));  // open: Carry_in
endmodule

module adder_8bit (
  input  Carry_in,
  input  [7:0] A,
  input  [7:0] B,
  output [7:0] Result,
  output Carry_out
);

  wire adder_4bit_1_out_5;

  // Probe on A
  // Probe on B
  adder_4bit adder_4bit_1 (
    .in_1(Carry_in), .in_2(A[3:0]), .in_3(B[3:0]), .out_4(Result[3:0]), .out_5(adder_4bit_1_out_5));
  adder_4bit adder_4bit_2 (
    .in_1(adder_4bit_1_out_5), .in_2(A[7:4]), .in_3(B[7:4]), .out_4(Result[7:4]), .out_5(Carry_out));
  // Probe on Result
  // Probe on Carry_out
endmodule

module adder_4bit (
  input  in_1,
  input  [3:0] in_2,
  input  [3:0] in_3,
  output [3:0] out_4,
  output out_5
);

  wire adder_2bit_1_out_5;

  // Probe on in_2
  // Probe on in_3
  adder_2bit adder_2bit_1 (
    .InitialCarry(in_1), .A(in_2[1:0]), .B(in_3[1:0]), .sum(out_4[1:0]), .out_5(adder_2bit_1_out_5));
  adder_2bit adder_2bit_2 (
    .InitialCarry(adder_2bit_1_out_5), .A(in_2[3:2]), .B(in_3[3:2]), .sum(out_4[3:2]), .out_5(out_5));
  // Probe on out_4
  // Probe on out_5
endmodule

module adder_2bit (
  input  InitialCarry,
  input  [1:0] A,
  input  [1:0] B,
  output [1:0] sum,
  output out_5
);

  wire adder_1bit_1_carry_out;

  adder_1bit adder_1bit_1 (
    .A(A[0]), .B(B[0]), .Carry_in(InitialCarry), .Sum(sum[0]), .Carry_out(adder_1bit_1_carry_out));
  // Probe on sum
  adder_1bit adder_1bit_2 (.A(A[1]), .B(B[1]), .Carry_in(adder_1bit_1_carry_out), .Sum(sum[1]), .Carry_out(out_5));
endmodule

module adder_1bit (
  input  A,
  input  B,
  input  Carry_in,
  output Sum,
  output Carry_out
);

  wire and_1_out, and_2_out, xor_1_out;

  xor xor_1 (xor_1_out, A, B);
  and and_1 (and_1_out, A, B);
  xor xor_2 (Sum, xor_1_out, Carry_in);
  and and_2 (and_2_out, xor_1_out, Carry_in);
  or or_1 (Carry_out, and_2_out, and_1_out);
endmodule

module adder_32bit (
  input  Carry_in,
  input  [31:0] First_Value,
  input  [31:0] Second_Value,
  output [31:0] Result,
  output Carry_out
);

  wire adder_8bit_1_carry_out, adder_8bit_2_carry_out, adder_8bit_3_carry_out;

  // Probe on First_Value
  // Probe on Second_Value
  // Probe on Carry_in
  adder_8bit adder_8bit_1 (
    .Carry_in(Carry_in), .A(First_Value[7:0]), .B(Second_Value[23:16]), .Result(Result[7:0]),
    .Carry_out(adder_8bit_1_carry_out));
  adder_8bit adder_8bit_2 (
    .Carry_in(adder_8bit_1_carry_out), .A(First_Value[15:8]), .B(Second_Value[15:8]), .Result(Result[15:8]),
    .Carry_out(adder_8bit_2_carry_out));
  adder_8bit adder_8bit_3 (
    .Carry_in(adder_8bit_2_carry_out), .A(First_Value[23:16]), .B(Second_Value[7:0]), .Result(Result[23:16]),
    .Carry_out(adder_8bit_3_carry_out));
  adder_8bit adder_8bit_4 (
    .Carry_in(adder_8bit_3_carry_out), .A(First_Value[31:24]), .B(Second_Value[31:24]),
    .Result(Result[31:24]), .Carry_out(Carry_out));
  // Probe on Result
endmodule

module sum_4val (
  input  [15:0] sum1,
  input  [15:0] sum2,
  input  [15:0] sum3,
  input  [15:0] sum4,
  output [15:0] result,
  output carry
);

  wire [15:0] adder_16bit_1_result, adder_16bit_2_result;

  adder_16bit adder_16bit_1 (.A(sum1), .B(sum2), .Result(adder_16bit_1_result));  // open: Carry_in, Carry_out
  adder_16bit adder_16bit_2 (.A(sum3), .B(sum4), .Result(adder_16bit_2_result));  // open: Carry_in, Carry_out
  adder_16bit adder_16bit_3 (
    .A(adder_16bit_1_result), .B(adder_16bit_2_result), .Result(result), .Carry_out(carry));  // open: Carry_in
endmodule

module test (
  input  in_1,
  input  [7:0] in_2
);

  wire clock_1_out, clock_2_out;
  wire [3:0] rom_1_data;
  wire [7:0] counter_1_q, counter_2_q, counter_3_q;
  wire [15:0] ram_1_dout, ram_2_dout;

  ROM #(.dataWidth(4)) rom_1 (.addr(counter_1_q), .data(rom_1_data));
  Counter counter_1 (.Q(counter_1_q), .clk(clock_1_out));  // open: load, D, count, carry, up, clr
  Clock clock_1 (.out(clock_1_out));
  Counter #(.max('hf)) counter_2 (
    .count(rom_1_data[3]), .Q(counter_2_q), .clk(clock_1_out));  // open: load, D, carry, up, clr
  Counter #(.max('hf)) counter_3 (
    .load(rom_1_data[1]), .D(8'h8), .count(rom_1_data[2]), .Q(counter_3_q), .clk(clock_1_out),
    .clr(rom_1_data[0]));  // open: carry, up
  RAM #(.dataWidth(16)) ram_1 (.addr(counter_2_q), .clk(clock_1_out), .dout(ram_1_dout));  // open: we, oe, din
  RAM #(.dataWidth(16)) ram_2 (.addr(counter_3_q), .clk(clock_1_out), .dout(ram_2_dout));  // open: we, oe, din
  // Probe on ram_1_dout
  // Probe on ram_2_dout
  Clock clock_2 (.out(clock_2_out));
  Counter counter_4 (.load(in_1), .D(in_2), .clk(clock_2_out));  // open: count, Q, carry, up, clr

  // Notes on the sheet:
  //   contents of rom_1 (hex, n*v repeats v):
  //   8*c 1 15*c e 8*c
endmodule
